// Logisim project pleasework - Copy.circ as structural Verilog: 4 circuits, main circuit jk
module jk (
  input  in_1,
  input  in_2,
  input  in_3,
  input  in_4,
  input  in_5,
  output out_6,
  output out_7
);

  wire nand_1_out, nand_2_out, not_1_out, not_2_out, not_3_out, not_4_out, not_5_out, not_6_out;

  nand nand_1 (nand_1_out, in_2, in_5, in_3, out_7);
  nand nand_2 (nand_2_out, out_6, in_3, in_1, in_4);
  not not_1 (not_1_out, in_1);
  not not_2 (not_2_out, nand_1_out);
  not not_3 (not_3_out, out_7);
  not not_4 (not_4_out, out_6);
  not not_5 (not_5_out, nand_2_out);
  not not_6 (not_6_out, in_5);
  or or_1 (out_6, not_1_out, not_2_out, not_3_out);
  or or_2 (out_7, not_4_out, not_5_out, not_6_out);
endmodule

module Sigment_decoder (
  input  iB,
  input  iC,
  input  iD,
  output A,
  output B,
  output C,
  output D,
  output E,
  output F,
  output G
);

  wire and_1_out, and_2_out, and_3_out, and_4_out, and_5_out, and_6_out, and_7_out, and_8_out, and_9_out,
       and_10_out, and_11_out, not_1_out, not_2_out, not_3_out, not_4_out, not_5_out, not_6_out, not_7_out,
       not_8_out;

  not not_1 (not_1_out, iB);
  not not_2 (not_2_out, iD);
  and and_1 (and_1_out, not_1_out, not_2_out);
  and and_2 (and_2_out, iB, iD);
  and and_3 (and_3_out, iC, iD);
  not not_3 (not_3_out, iC);
  not not_4 (not_4_out, iD);
  not not_5 (not_5_out, iD);
  not not_6 (not_6_out, iB);
  not not_7 (not_7_out, iC);
  not not_8 (not_8_out, iD);
  and and_4 (and_4_out, not_3_out, not_4_out);
  and and_5 (and_5_out, iB, iC);
  and and_6 (and_6_out, iC, not_5_out);
  and and_7 (and_7_out, not_6_out, iC);
  and and_8 (and_8_out, not_7_out, iD, iB);
  and and_9 (and_9_out, not_7_out, iB);
  and and_10 (and_10_out, not_8_out, iB);
  and and_11 (and_11_out, not_8_out, iC);
  or or_1 (A, and_1_out, iC, and_2_out);
  or or_2 (B, not_1_out, and_3_out, and_4_out);
  or or_3 (C, not_3_out, iD, and_5_out);
  or or_4 (D, and_1_out, and_6_out, and_7_out, and_8_out);
  or or_5 (E, and_1_out, and_6_out);
  or or_6 (F, and_4_out, and_9_out, and_10_out);
  or or_7 (G, and_9_out, and_7_out, and_11_out);

  // Notes on the sheet:
  //   b
  //   c
  //   d
  //   A
  //   B
  //   C
  //   D
  //   E
  //   F
  //   G
endmodule

module test (
  input  in_1,
  input  in_2,
  input  keyslot,
  input  Motion_sensor,
  input  in_5,
  input  in_6,
  input  manual,
  input  in_8,
  input  in_9,
  input  in_10,
  input  in_11,
  input  in_12,
  input  in_13,
  input  in_14,
  input  in_15,
  input  in_16,
  input  in_17,
  input  in_18,
  input  in_19
);

  wire alarm, and_1_out, and_2_out, and_3_out, and_5_out, and_6_out, and_8_out, and_9_out, and_10_out,
       and_11_out, clock_1_out, correct, d_ff_2_q, d_ff_3_q, false, ib, ic, id, j_k_ff_1_qn, j_k_ff_2_qn,
       jk2bitcounter_1_q0, jk2bitcounter_1_q1, not_2_out, not_3_out, not_4_out, not_5_out, not_6_out,
       not_7_out, or_1_out, or_2_out, or_4_out, ready, RESET, Send_out, sigment_decoder_1_a,
       sigment_decoder_1_b, sigment_decoder_1_c, sigment_decoder_1_d, sigment_decoder_1_e,
       sigment_decoder_1_f, sigment_decoder_1_g, sigment_decoder_2_a, sigment_decoder_2_b,
       sigment_decoder_2_c, sigment_decoder_2_d, sigment_decoder_2_e, sigment_decoder_2_f,
       sigment_decoder_2_g, stop, test, xnor_1_out, xnor_2_out, xnor_3_out, xnor_4_out, xnor_5_out,
       xnor_6_out, xnor_7_out, xnor_8_out;

  xnor xnor_1 (xnor_1_out, in_1, in_12);
  xnor xnor_2 (xnor_2_out, in_2, in_13);
  xnor xnor_3 (xnor_3_out, in_5, in_14);
  xnor xnor_4 (xnor_4_out, in_6, in_15);
  xnor xnor_5 (xnor_5_out, in_8, in_16);
  xnor xnor_6 (xnor_6_out, in_9, in_17);
  xnor xnor_7 (xnor_7_out, in_10, in_18);
  xnor xnor_8 (xnor_8_out, in_11, in_19);
  and and_1 (and_1_out, xnor_1_out, xnor_2_out, xnor_3_out, xnor_4_out, xnor_5_out, xnor_6_out, xnor_7_out, xnor_8_out);
  LED led_1 (.in(correct));
  Button Send (.out(Send_out));
  and and_2 (and_2_out, test, false);
  not not_1 (ready, or_1_out);
  or or_1 (or_1_out, ic, ib, id);
  not not_2 (not_2_out, alarm);
  Sigment_decoder sigment_decoder_1 (
    .iB(ib), .iC(ic), .iD(id), .A(sigment_decoder_1_a), .B(sigment_decoder_1_b), .C(sigment_decoder_1_c),
    .D(sigment_decoder_1_d), .E(sigment_decoder_1_e), .F(sigment_decoder_1_f), .G(sigment_decoder_1_g));
  D_Flip_Flop d_ff_1 (.D(and_2_out), .clk(and_2_out), .Q(stop), .reset(d_ff_2_q));  // open: Qn, preset
  D_Flip_Flop d_ff_2 (.D(ready), .clk(ready), .Q(d_ff_2_q), .reset(d_ff_2_q));  // open: Qn, preset
  LED led_2 (.in(ready));
  not not_3 (not_3_out, stop);
  LED led_3 (.in(and_3_out));
  and and_3 (and_3_out, not_4_out, not_5_out);
  not not_4 (not_4_out, ready);
  Clock clock_1 (.out(clock_1_out));
  not not_5 (not_5_out, correct);
  and and_4 (test, Send_out, not_2_out, not_3_out);
  LED led_4 (.in(alarm));
  and and_5 (and_5_out, stop, clock_1_out);
  LED led_5 (.in(alarm));
  LED led_6 (.in(alarm));
  _7_Segment_Display u_7_segment_display_1 (
    .g(sigment_decoder_1_g), .f(sigment_decoder_1_f), .a(sigment_decoder_1_a), .b(sigment_decoder_1_b),
    .e(sigment_decoder_1_e), .d(sigment_decoder_1_d), .c(sigment_decoder_1_c));  // open: dp
  J_K_Flip_Flop j_k_ff_1 (.J(stop), .K(stop), .clk(and_5_out), .Q(id), .Qn(j_k_ff_1_qn));  // open: preset, reset
  D_Flip_Flop d_ff_3 (.D(and_1_out), .clk(test), .Q(d_ff_3_q), .reset(RESET));  // open: Qn, preset
  Button button_1 (.out(RESET));
  J_K_Flip_Flop j_k_ff_2 (
    .J(j_k_ff_1_qn), .K(j_k_ff_1_qn), .clk(and_5_out), .Q(ic), .Qn(j_k_ff_2_qn));  // open: preset, reset
  not not_6 (not_6_out, d_ff_3_q);
  or or_2 (or_2_out, d_ff_3_q, RESET);
  and and_6 (and_6_out, j_k_ff_1_qn, j_k_ff_2_qn);
  J_K_Flip_Flop j_k_ff_3 (.J(and_6_out), .K(and_6_out), .clk(and_5_out), .Q(ib));  // open: Qn, preset, reset
  and and_7 (correct, d_ff_3_q, keyslot);
  and and_8 (and_8_out, keyslot, not_6_out);
  Sigment_decoder sigment_decoder_2 (
    .iC(jk2bitcounter_1_q1), .iD(jk2bitcounter_1_q0), .A(sigment_decoder_2_a), .B(sigment_decoder_2_b),
    .C(sigment_decoder_2_c), .D(sigment_decoder_2_d), .E(sigment_decoder_2_e), .F(sigment_decoder_2_f),
    .G(sigment_decoder_2_g));  // open: iB
  _7_Segment_Display u_7_segment_display_2 (
    .g(sigment_decoder_2_g), .f(sigment_decoder_2_f), .a(sigment_decoder_2_a), .b(sigment_decoder_2_b),
    .e(sigment_decoder_2_e), .d(sigment_decoder_2_d), .c(sigment_decoder_2_c));  // open: dp
  jk2bitCounter jk2bitcounter_1 (
    .i(and_8_out), .clk(test), .r(or_2_out), .q0(jk2bitcounter_1_q0), .q1(jk2bitcounter_1_q1));
  not not_7 (not_7_out, keyslot);
  and and_9 (and_9_out, not_7_out, Motion_sensor);
  and and_10 (and_10_out, jk2bitcounter_1_q1, jk2bitcounter_1_q0);
  or or_3 (false, jk2bitcounter_1_q0, jk2bitcounter_1_q1);
  or or_4 (or_4_out, Motion_sensor, manual);
  and and_11 (and_11_out, or_4_out, correct);
  or or_5 (alarm, and_9_out, and_10_out);
  LED led_7 (.in(and_11_out));
  LED led_8 (.in(and_11_out));

  // Other names for the same wires on the sheet: key = keyslot

  // Notes on the sheet:
  //   Enter
  //   Alarm (calling 911)
  //   key slot
  //   leds (room light)
  //   Air conditioner
endmodule

module jk2bitCounter (
  input  i,
  input  clk,
  input  r,
  output q0,
  output q1
);

  J_K_Flip_Flop j_k_ff_1 (.J(i), .K(i), .clk(clk), .Q(q0), .reset(r));  // open: Qn, preset
  J_K_Flip_Flop j_k_ff_2 (.J(q0), .K(q0), .clk(clk), .Q(q1), .reset(r));  // open: Qn, preset
endmodule
